# Fritzing sketch DS18B20Carrier (saved by Fritzing 0.9.3b)
circuit board: 4.00135cm x 2cm
breadboards: 1

parts:
  4_7k = Resistor [tolerance=±5% resistance=4.7k package=THT]
  DS18B20 = male pin header, 3 pins [form="♂ (male)"]
  Clips = male pin header, 3 pins [form="♂ (male)"]
  3v = Pad [width=5.4000000000000004 height=10 connect=north]
  GND = Pad [width=5.4000000000000004 height=10 connect=north]
  3v1 = Pad [width=5.4000000000000004 height=10 connect=north]
  GND1 = Pad [width=5.4000000000000004 height=10 connect=north]

nets:
  N1: 4_7k.Pin_0, DS18B20.pin1, Clips.pin1
  N2: 4_7k.Pin_1, DS18B20.pin2, Clips.pin2, 3v.pad, 3v1.pad
  N3: DS18B20.pin3, Clips.pin3, GND.pad, GND1.pad

notes:
  Y
  R
  B
  3v
  gnd
